// Logisim project DDCA-PROBLEM 1 CIRCUIT.circ as structural Verilog: 1 circuit, main circuit main
module main (
  input  A,
  input  B,
  output Z
);

  wire AND_out, NOT_out, OR_out;

  not NOT (NOT_out, A);
  or OR (OR_out, A, B);
  and AND (AND_out, NOT_out, OR_out);
  or or_2 (Z, AND_out, OR_out);
endmodule
