// Logisim project DDCA-PROBLEM 2 CIRCUIT.circ as structural Verilog: 1 circuit, main circuit main
// Y
module main (
  input  in_1,
  input  in_2,
  output out_3
);

  wire AND_2_out, AND_out, not_1_out, not_2_out;

  not not_1 (not_1_out, in_1);
  not not_2 (not_2_out, in_2);
  and AND (AND_out, in_2, not_1_out);
  and AND_2 (AND_2_out, not_2_out, in_1);
  or OR (out_3, AND_out, AND_2_out);
endmodule
