// Logisim project DDCA-PROBLEM 3 CIRCUIT.circ as structural Verilog: 1 circuit, main circuit main
module main (
  input  A,
  input  B,
  input  C,
  output Y
);

  wire NAND_out, NOT_out;

  not NOT (NOT_out, C);
  nand NAND (NAND_out, A, B);
  and AND (Y, NAND_out, B, NOT_out);
endmodule
