// Logisim project DDCA-SEP1ST.circ as structural Verilog: 1 circuit, main circuit main
module main (
  input  l0,
  input  i1,
  input  in_3
);

  wire multiplexer_1_out;

  Multiplexer multiplexer_1 (.in0(l0), .in1(i1), .out(multiplexer_1_out), .sel(in_3));  // open: en
  LED y (.in(multiplexer_1_out));
endmodule
