// Logisim project DDCA.....circ as structural Verilog: 1 circuit, main circuit main
module main (
  input  in_1,
  input  l0,
  input  l1,
  input  in_4,
  input  in_5,
  input  in_6,
  input  in_7,
  input  l2,
  input  in_9,
  input  l3,
  input  in_11,
  input  in_12,
  input  [1:0] S0S1,
  input  in_14,
  input  S,
  input  in_16,
  input  [1:0] in_17,
  input  [2:0] in_18,
  input  in_19,
  input  _0,
  input  [1:0] in_21,
  input  in_22,
  input  [2:0] in_23,
  input  in_24,
  input  _1,
  input  in_26,
  input  in_27,
  input  _2,
  input  _3,
  input  ENABLE,
  input  in_31,
  input  in_32,
  input  in_33,
  input  in_34,
  input  [2:0] in_35,
  input  in_36,
  output out_37,
  output out_38,
  output out_39,
  output out_40,
  output out_41,
  output out_42
);

  wire demultiplexer_1_out0, demultiplexer_1_out1, demultiplexer_1_out2, demultiplexer_1_out3,
       demultiplexer_1_out4, demultiplexer_1_out5, demultiplexer_1_out6, demultiplexer_1_out7,
       demultiplexer_3_out0, demultiplexer_3_out1, demultiplexer_4_out0, demultiplexer_4_out1,
       demultiplexer_4_out2, demultiplexer_4_out3, multiplexer_1_out, multiplexer_2_out, undriven,
       undriven_2, undriven_3;
  wire [1:0] priority_encoder_1_out;
  wire [2:0] priority_encoder_2_out;

  Multiplexer #(.select(2)) multiplexer_1 (
    .in0(l0), .in1(l1), .in2(l2), .in3(l3), .out(multiplexer_1_out), .sel(S0S1));  // open: en
  Demultiplexer #(.select(3)) demultiplexer_1 (
    .out0(demultiplexer_1_out0), .out1(demultiplexer_1_out1), .out2(demultiplexer_1_out2),
    .out3(demultiplexer_1_out3), .out4(demultiplexer_1_out4), .out5(demultiplexer_1_out5),
    .out6(demultiplexer_1_out6), .out7(demultiplexer_1_out7), .in(in_24), .sel(in_35));  // open: en
  LED y (.in(multiplexer_1_out));
  LED led_1 (.in(demultiplexer_1_out0));
  LED led_2 (.in(demultiplexer_1_out1));
  LED led_3 (.in(demultiplexer_1_out2));
  LED led_4 (.in(demultiplexer_1_out3));
  LED led_5 (.in(demultiplexer_1_out4));
  LED led_6 (.in(demultiplexer_1_out5));
  LED led_7 (.in(demultiplexer_1_out6));
  LED led_8 (.in(demultiplexer_1_out7));
  Multiplexer #(.select(3)) multiplexer_2 (
    .in0(in_1), .in1(in_4), .in2(in_6), .in3(in_9), .in4(in_11), .in5(in_12), .in6(in_14), .in7(in_16),
    .out(multiplexer_2_out), .sel(in_18));  // open: en
  LED led_9 (.in(multiplexer_2_out));
  Priority_Encoder #(.select(2)) priority_encoder_1 (
    .in0(_0), .in1(_1), .in2(_2), .in3(_3), .out(priority_encoder_1_out), .gs(out_38), .en_in(undriven_2));  // open: en_out
  Demultiplexer #(.select(2)) demultiplexer_2 (
    .out0(out_39), .out1(out_40), .out2(out_41), .out3(out_42), .in(undriven));  // open: sel, en
  Demultiplexer demultiplexer_3 (
    .out0(demultiplexer_3_out0), .out1(demultiplexer_3_out1), .in(in_5), .sel(S));  // open: en
  LED u_l0 (.in(demultiplexer_3_out0));
  LED u_l1 (.in(demultiplexer_3_out1));
  Demultiplexer #(.select(2)) demultiplexer_4 (
    .out0(demultiplexer_4_out0), .out1(demultiplexer_4_out1), .out2(demultiplexer_4_out2),
    .out3(demultiplexer_4_out3), .in(in_7), .sel(in_17));  // open: en
  Priority_Encoder priority_encoder_2 (
    .in0(in_19), .in1(in_22), .in2(in_26), .in3(in_27), .in4(in_31), .in5(in_33), .in6(in_34), .in7(in_36),
    .out(priority_encoder_2_out), .en_in(undriven_3));  // open: gs, en_out
  LED led_10 (.in(demultiplexer_4_out0));
  LED led_11 (.in(demultiplexer_4_out1));
  LED led_12 (.in(demultiplexer_4_out2));
  LED led_13 (.in(demultiplexer_4_out3));
endmodule
