// Logisim project HC03C.circ as structural Verilog: 1 circuit, main circuit main
module main (
  input  A,
  input  B,
  output Sum,
  output C_Out
);

  xor XOR1 (Sum, A, B);
  and AND1 (C_Out, A, B);
endmodule
