// Logisim project IMPLEMENTATION OF BOOLEAN EXPRESSION-DDCA.circ as structural Verilog: 1 circuit, main circuit main
module main (
  input  A,
  input  B,
  output F1
);

  wire and_1_out, and_2_out, not_1_out;

  not not_1 (not_1_out, A);
  and and_1 (and_1_out, not_1_out, B);
  buf and_2 (and_2_out, A);  // AND_Gate
  or or_1 (F1, and_1_out, and_2_out);
endmodule
