// Logisim project NAND GATE.circ as structural Verilog: 1 circuit, main circuit main
module main (
  input  A,
  input  B,
  output A_NAND_B
);

  // AND_Gate and_1 has open pins: in0=A, in1=B, out=open
  nand nand_1 (A_NAND_B, A, B);
endmodule
